# Fritzing sketch Component Diagram (saved by Fritzing 1.0.2b)

parts:
  Hbridge_front_linear_actuators = H-Bridge with L298N
  Hbridge_for_left_motors = H-Bridge with L298N
  Hbridge_for_right_motors = H-Bridge with L298N
  Part1 = Arduino Mega 2560 (Rev3)
  M3 = linear actuator [package=THT]
  M4 = linear actuator [package=THT]
  M5 = linear actuator [package=THT]
  M6 = linear actuator [package=THT]
  Hbridge_for_middle_motors = H-Bridge with L298N
  DC_Mot_Enc1 = DC Motor with two-phase hall-encoder [part_number=VT-E-G25A-06-177E]
  DC_Mot_Enc2 = DC Motor with two-phase hall-encoder [part_number=VT-E-G25A-06-177E]
  DC_Mot_Enc3 = DC Motor with two-phase hall-encoder [part_number=VT-E-G25A-06-177E]
  DC_Mot_Enc4 = DC Motor with two-phase hall-encoder [part_number=VT-E-G25A-06-177E]
  DC_Mot_Enc5 = DC Motor with two-phase hall-encoder [part_number=VT-E-G25A-06-177E]
  DC_Mot_Enc6 = DC Motor with two-phase hall-encoder [part_number=VT-E-G25A-06-177E]
  DC_Mot_Enc7 = DC Motor with two-phase hall-encoder [part_number=VT-E-G25A-06-177E]
  DC_Mot_Enc8 = DC Motor with two-phase hall-encoder [part_number=VT-E-G25A-06-177E]
  Part2 = Adafruit VL530X Time of Flight Distance Sensor [part_number="Adafruit #3317"]
  JL012-13-5_1 = JL012-13-5.2 Lever (Limit) Switch SPDT + NO + NC [part_number=JL012-13-5.2]
  JL012-13-5_2 = JL012-13-5.2 Lever (Limit) Switch SPDT + NO + NC [part_number=JL012-13-5.2]
  JL012-13-5_3 = JL012-13-5.2 Lever (Limit) Switch SPDT + NO + NC [part_number=JL012-13-5.2]
  JL012-13-5_4 = JL012-13-5.2 Lever (Limit) Switch SPDT + NO + NC [part_number=JL012-13-5.2]
  M7 = fc-51 [package=THT]
  U2 = LIPO-1000mAh [package=lipo-1000]
  U1 = LIPO-1000mAh [package=lipo-1000]
  U4 = LIPO-1000mAh [package=lipo-1000]
  U3 = LIPO-1000mAh [package=lipo-1000]
  Hbridge_rear_linear_actuators = H-Bridge with L298N

nets:
  12V: Hbridge_front_linear_actuators.12V, Hbridge_for_left_motors.12V, Hbridge_for_right_motors.12V, Hbridge_for_middle_motors.12V, U2.+, U1.+, U4.+, U3.+, Hbridge_rear_linear_actuators.12V
  GND: Hbridge_front_linear_actuators.GND, Hbridge_for_left_motors.GND, Hbridge_for_right_motors.GND, Hbridge_for_middle_motors.GND, U2.-, U1.-, U4.-, U3.-, Hbridge_rear_linear_actuators.GND
  N1: Hbridge_front_linear_actuators.ENA, Part1.D7_PWM
  N2: Hbridge_front_linear_actuators.IN1, Part1.D43
  N3: Hbridge_front_linear_actuators.IN2, Part1.D45
  N4: Hbridge_front_linear_actuators.IN3, Part1.D39
  N5: Hbridge_front_linear_actuators.IN4, Part1.D41
  N6: Hbridge_front_linear_actuators.ENB, Part1.D6_PWM
  N7: Hbridge_front_linear_actuators.M1-01, M3.pin2
  N8: Hbridge_front_linear_actuators.M1-02, M3.pin1
  N9: Hbridge_front_linear_actuators.M2-01, M4.pin1
  N10: Hbridge_front_linear_actuators.M2-02, M4.pin2
  N11: Hbridge_for_left_motors.ENA, Part1.D11_PWM
  N12: Hbridge_for_left_motors.IN1, Part1.D40
  N13: Hbridge_for_left_motors.IN2, Part1.D38
  N14: Hbridge_for_left_motors.IN3, Part1.D36
  N15: Hbridge_for_left_motors.IN4, Part1.D34
  N16: Hbridge_for_left_motors.ENB, Part1.D10_PWM
  N17: Hbridge_for_left_motors.M1-01, DC_Mot_Enc7.pin2
  N18: Hbridge_for_left_motors.M1-02, DC_Mot_Enc7.pin1
  N19: Hbridge_for_left_motors.M2-01, DC_Mot_Enc8.pin1
  N20: Hbridge_for_left_motors.M2-02, DC_Mot_Enc8.pin2
  N21: Hbridge_for_right_motors.ENA, Hbridge_for_right_motors.ENA-5V, Part1.D13_PWM
  N22: Hbridge_for_right_motors.IN1, Part1.D22
  N23: Hbridge_for_right_motors.IN2, Part1.D24
  N24: Hbridge_for_right_motors.IN3, Part1.D26
  N25: Hbridge_for_right_motors.IN4, Part1.D28
  N26: Hbridge_for_right_motors.ENB, Hbridge_for_right_motors.ENB-5V, Part1.D12_PWM
  N27: Hbridge_for_right_motors.M1-01, DC_Mot_Enc6.pin2
  N28: Hbridge_for_right_motors.M1-02, DC_Mot_Enc6.pin1
  N29: Hbridge_for_right_motors.M2-01, DC_Mot_Enc5.pin1
  N30: Hbridge_for_right_motors.M2-02, DC_Mot_Enc5.pin2
  N31: Part1.D21/SCL, Part1.SCL, Part2.SCL
  N32: Part1.D20/SDA, Part1.SDA, Part2.SDA
  N33: Part1.D9_PWM, Hbridge_for_middle_motors.ENA
  N34: Part1.D8_PWM, Hbridge_for_middle_motors.ENB
  5V: Part1.5V, DC_Mot_Enc6.pin5, DC_Mot_Enc8.pin5, Part2.VCC, M7.pin3
  GND_2: Part1.GND, DC_Mot_Enc6.pin4, DC_Mot_Enc8.pin4, Part2.GND, JL012-13-5_1.C, JL012-13-5_2.C, JL012-13-5_3.C, JL012-13-5_4.C, M7.pin2
  N35: Part1.D2_PWM, DC_Mot_Enc6.pin3
  N36: Part1.D3_PWM, DC_Mot_Enc8.pin3
  N37: Part1.D4_PWM, Hbridge_rear_linear_actuators.ENB
  N38: Part1.D5_PWM, Hbridge_rear_linear_actuators.ENA
  N39: Part1.D30, DC_Mot_Enc6.pin6
  N40: Part1.D31, Hbridge_for_middle_motors.IN4, Hbridge_for_middle_motors.ENB-5V
  N41: Part1.D32, DC_Mot_Enc8.pin6
  N42: Part1.D33, Hbridge_for_middle_motors.IN3
  N43: Part1.D35, Hbridge_for_middle_motors.IN2
  N44: Part1.D37, Hbridge_for_middle_motors.IN1
  N45: Part1.D44, M7.pin1
  N46: Part1.D46, JL012-13-5_1.NO
  N47: Part1.D47, Hbridge_rear_linear_actuators.IN1
  N48: Part1.D48, JL012-13-5_4.NO
  N49: Part1.D49, Hbridge_rear_linear_actuators.IN2
  N50: Part1.D50, JL012-13-5_2.NO
  N51: Part1.D51, Hbridge_rear_linear_actuators.IN3
  N52: Part1.D52, JL012-13-5_3.NO
  N53: Part1.D53, Hbridge_rear_linear_actuators.IN4
  N54: M5.pin1, Hbridge_rear_linear_actuators.M1-02
  N55: M5.pin2, Hbridge_rear_linear_actuators.M1-01
  N56: M6.pin1, Hbridge_rear_linear_actuators.M2-01
  N57: M6.pin2, Hbridge_rear_linear_actuators.M2-02
  N58: Hbridge_for_middle_motors.M1-01, DC_Mot_Enc3.pin2, DC_Mot_Enc4.pin2
  N59: Hbridge_for_middle_motors.M1-02, DC_Mot_Enc3.pin1, DC_Mot_Enc4.pin1
  N60: Hbridge_for_middle_motors.M2-01, DC_Mot_Enc1.pin1, DC_Mot_Enc2.pin1
  N61: Hbridge_for_middle_motors.M2-02, DC_Mot_Enc1.pin2, DC_Mot_Enc2.pin2

custom parts:
  H-Bridge with L298N: h-bridge
  linear actuator: Generic linear actuator.
  Adafruit VL530X Time of Flight Distance Sensor: The VL53L0X is a Time of Flight distance sensor like no other you've used! The sensor contains a very tiny invisible laser source, and a matching sensor. The VL53L0X can detect the "time of flight", or how long the light has taken to bounce back to the sensor. Since it uses a very narrow light source, it is good for determining distance of only the surface directly in front of it. Unlike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
  JL012-13-5.2 Lever (Limit) Switch SPDT + NO + NC: Micro Switch; Model No.: JL012-13.5-2; Actuator Action: Momentary; Actuator Type: Hinge Lever; Contact Configuration: 1NO, 1NC (SPDT) Temperature -25~65℃；Relative humidity: below 85%; Rate Voltage: 125V AC; Rated Current: 1A.
